// Logisim project tarea-multiple-unidad4-sergio-garcia.circ as structural Verilog: 1 circuit, main circuit main
// B1) Dos MUX 4x1
module main (
  input  C1,
  input  C0,
  input  E0,
  input  E1,
  input  E2,
  input  E3,
  input  C2,
  input  C3,
  input  C4,
  input  D0,
  input  D1,
  input  D2,
  input  D3,
  input  D4,
  input  D5,
  input  D6,
  input  D7,
  input  in_18,
  input  in_19,
  input  in_20,
  input  in_21,
  input  in_22,
  input  in_23,
  output S,
  output out_25
);

  wire and_1_out, and_2_out, and_3_out, and_4_out, and_5_out, and_6_out, and_7_out, and_8_out, and_9_out,
       and_10_out, and_11_out, and_12_out, and_13_out, and_14_out, and_15_out, and_16_out, and_17_out,
       clock_1_out, clock_2_out, j_k_ff_1_q, j_k_ff_2_q, not_1_out, not_2_out, not_3_out, not_4_out,
       not_5_out, not_6_out, not_7_out, or_3_out, or_4_out, S2_out;

  Clock clock_1 (.out(clock_1_out));
  J_K_Flip_Flop j_k_ff_1 (
    .J(j_k_ff_2_q), .K(j_k_ff_2_q), .clk(clock_1_out), .Q(j_k_ff_1_q));  // open: Qn, preset, reset
  J_K_Flip_Flop j_k_ff_2 (.J(in_18), .K(in_19), .clk(clock_1_out), .Q(j_k_ff_2_q));  // open: Qn, preset, reset
  not not_1 (not_1_out, C1);
  not not_2 (not_2_out, C2);
  Clock clock_2 (.out(clock_2_out));
  not not_3 (not_3_out, C0);
  not not_4 (not_4_out, C3);
  and and_1 (and_1_out, j_k_ff_1_q, j_k_ff_2_q);
  and and_2 (and_2_out, not_3_out, not_1_out, E0);
  and and_3 (and_3_out, not_1_out, C0, E1);
  and and_4 (and_4_out, not_3_out, C1, E2);
  and and_5 (and_5_out, C0, C1, E3);
  not not_5 (not_5_out, C4);
  or or_1 (S, and_2_out, and_3_out, and_4_out, and_5_out);
  and and_6 (and_6_out, not_2_out, not_4_out, D0, not_5_out);
  and and_7 (and_7_out, not_2_out, not_4_out, D1, C4);
  and and_8 (and_8_out, not_5_out, C3, not_2_out, D2);
  and and_9 (and_9_out, C4, C3, not_2_out, D3);
  and and_10 (and_10_out, C2, not_4_out, not_5_out, D4);
  and and_11 (and_11_out, C2, not_4_out, C4, D5);
  and and_12 (and_12_out, C2, C3, not_5_out, D6);
  and and_13 (and_13_out, C2, C3, C4, D7);
  not not_6 (not_6_out, and_1_out);
  not not_7 (not_7_out, and_1_out);
  and and_14 (and_14_out, not_7_out, not_6_out, in_20);
  and and_15 (and_15_out, not_6_out, and_1_out, in_21);
  and and_16 (and_16_out, not_7_out, and_1_out, in_22);
  and and_17 (and_17_out, and_1_out, and_1_out, in_23);
  or or_2 (out_25, and_6_out, and_7_out, and_8_out, and_9_out, and_10_out, and_11_out, and_12_out, and_13_out);
  or S2 (S2_out, and_15_out, and_16_out, and_17_out);
  or or_3 (or_3_out, and_14_out, and_17_out);
  or or_4 (or_4_out, and_14_out, and_16_out, and_17_out);
  Hex_Digit_Display HEX ();  // open: value, dp

  // Notes on the sheet:
  //   B) Multiplexor 8x1
  //   3) Ejercicio máquina de café
  //   A) Circuito que simule un multiplexor 4x1 (E0-E3 como entradas, S como salida y C0 y C1 como selectores
endmodule
